// Logisim project PROJETO2 (1).circ as structural Verilog: 8 circuits, main circuit InstructionFetch
module InstructionFetch (
  input  [31:0] in_1,
  input  in_2,
  output [31:0] SOMA,
  output [5:0] out_4,
  output [25:0] _0_25,
  output [15:0] _0_16,
  output [4:0] _12_16,
  output [4:0] _17_20,
  output [4:0] _21_25,
  output [5:0] _26_31
);

  wire clock_1_out;

  Hex_Digit_Display hex_digit_display_1 (.value(in_1[31:28]));  // open: dp
  Hex_Digit_Display hex_digit_display_2 (.value(_26_31[5:2]));  // open: dp
  Hex_Digit_Display hex_digit_display_3 (.value(in_1[27:24]));  // open: dp
  Hex_Digit_Display hex_digit_display_4 (.value({_26_31[1:0], _0_25[25:24]}));  // open: dp
  Hex_Digit_Display hex_digit_display_5 (.value(in_1[19:16]));  // open: dp
  Hex_Digit_Display hex_digit_display_6 (.value(in_1[23:20]));  // open: dp
  Hex_Digit_Display hex_digit_display_7 (.value(_0_25[19:16]));  // open: dp
  Hex_Digit_Display hex_digit_display_8 (.value(_0_25[23:20]));  // open: dp
  Hex_Digit_Display hex_digit_display_9 (.value(in_1[15:12]));  // open: dp
  Hex_Digit_Display hex_digit_display_10 (.value(_0_16[15:12]));  // open: dp
  Hex_Digit_Display hex_digit_display_11 (.value(in_1[11:8]));  // open: dp
  Hex_Digit_Display hex_digit_display_12 (.value(in_1[7:4]));  // open: dp
  Clock clock_1 (.out(clock_1_out));
  Hex_Digit_Display hex_digit_display_13 (.value(_0_16[11:8]));  // open: dp
  Hex_Digit_Display hex_digit_display_14 (.value(_0_16[7:4]));  // open: dp
  Hex_Digit_Display hex_digit_display_15 (.value(in_1[3:0]));  // open: dp
  Adder #(.width(32)) adder_1 (.a(in_1), .b({_26_31, _0_25[25:16], _0_16}), .out(SOMA));  // open: cin, cout
  Register #(.width(32)) register_1 (
    .D(SOMA), .en(1'b1), .Q({_26_31, _0_25[25:16], _0_16}), .clk(clock_1_out), .clr(in_2));
  Hex_Digit_Display hex_digit_display_16 (.value(_0_16[3:0]));  // open: dp
  RAM #(.addrWidth(16), .dataWidth(32)) ram_1 (.addr(_0_16));  // open: data, sel, clk, ld, clr
  RAM #(.addrWidth(16), .dataWidth(32)) ram_2 (.addr({_26_31, _0_25[25:16]}));  // open: data, sel, clk, ld, clr

  assign _0_25[15:0] = _0_16;
  assign _12_16 = _0_16[15:11];
  assign _17_20 = _0_25[20:16];
  assign _21_25 = _0_25[25:21];
  assign out_4 = _0_16[5:0];
endmodule

module Datapath_R (
  input  in_1
);

  wire and_1_out, clock_1_out, controle_1_alusrc, controle_1_branch, controle_1_escrita_mem,
       controle_1_escrita_reg, controle_1_jump, controle_1_leitura_mem, controle_1_mem_reg,
       controle_1_opalu0, controle_1_opalu1, controle_1_regdst, multiplexer_3_out, ula_1_out_4;
  wire [2:0] controleula_1_out_4;
  wire [4:0] instructionfetch_1__12_16, instructionfetch_1__17_20, instructionfetch_1__21_25,
       multiplexer_1_out;
  wire [5:0] instructionfetch_1__26_31, instructionfetch_1_out_4;
  wire [15:0] instructionfetch_1__0_16;
  wire [25:0] instructionfetch_1__0_25;
  wire [31:0] adder_1_out, banco_de_registradores_1_rx, banco_de_registradores_1_ry, bit_extender_1_out,
       instructionfetch_1_soma, multiplexer_2_out, multiplexer_4_out, multiplexer_6_out, shifter_1_out,
       ula_1_saida, undriven;

  InstructionFetch instructionfetch_1 (
    .in_1(multiplexer_6_out), .in_2(clock_1_out), .SOMA(instructionfetch_1_soma),
    .out_4(instructionfetch_1_out_4), ._0_25(instructionfetch_1__0_25), ._0_16(instructionfetch_1__0_16),
    ._12_16(instructionfetch_1__12_16), ._17_20(instructionfetch_1__17_20),
    ._21_25(instructionfetch_1__21_25), ._26_31(instructionfetch_1__26_31));
  Clock clock_1 (.out(clock_1_out));
  Controle controle_1 (
    .in_1(instructionfetch_1__26_31), .RegDST(controle_1_regdst), .ALUsrc(controle_1_alusrc),
    .mem_reg(controle_1_mem_reg), .escrita_reg(controle_1_escrita_reg), .leitura_mem(controle_1_leitura_mem),
    .Escrita_Mem(controle_1_escrita_mem), .Branch(controle_1_branch), .OpALU1(controle_1_opalu1),
    .OpALU0(controle_1_opalu0), .JUMP(controle_1_jump));
  Banco_de_Registradores banco_de_registradores_1 (
    .RY(banco_de_registradores_1_ry), .in_1(instructionfetch_1__21_25), .RX(banco_de_registradores_1_rx),
    .in_2(instructionfetch_1__17_20), .DATAIN(ula_1_saida), .WRITER(controle_1_escrita_reg),
    .DadosDemux(multiplexer_1_out));
  Multiplexer #(.width(5), .enable("false")) multiplexer_1 (
    .in0(instructionfetch_1__17_20), .in1(instructionfetch_1__12_16), .out(multiplexer_1_out),
    .sel(controle_1_regdst));
  Multiplexer #(.width(32), .enable("false")) multiplexer_2 (
    .in0(banco_de_registradores_1_rx), .in1(bit_extender_1_out), .out(multiplexer_2_out),
    .sel(controle_1_alusrc));
  assign bit_extender_1_out = {{16{1'b0}}, instructionfetch_1__0_16};  // Bit_Extender bit_extender_1
  ControleULA controleula_1 (
    .in_3(instructionfetch_1_out_4), .in_1(controle_1_opalu0), .in_2(controle_1_opalu1),
    .out_4(controleula_1_out_4));
  ULA ula_1 (
    .x(banco_de_registradores_1_ry), .y(multiplexer_2_out), .MUX(controleula_1_out_4), .out_4(ula_1_out_4),
    .saida(ula_1_saida));
  and and_1 (and_1_out, controle_1_branch, ula_1_out_4);
  Shifter #(.width(32)) shifter_1 (.in(bit_extender_1_out), .\dist (5'b00010), .out(shifter_1_out));
  Multiplexer #(.enable("false")) multiplexer_3 (
    .in0(controle_1_leitura_mem), .in1(controle_1_escrita_mem), .out(multiplexer_3_out), .sel(in_1));
  Adder #(.width(32)) adder_1 (.a(instructionfetch_1_soma), .b(shifter_1_out), .out(adder_1_out));  // open: cin, cout
  Memoria_de_Dados memoria_de_dados_1 (.in_1(ula_1_saida), .R_W(multiplexer_3_out), .saida(undriven));
  Multiplexer #(.width(32), .enable("false")) multiplexer_4 (
    .in0(instructionfetch_1_soma), .in1(adder_1_out), .out(multiplexer_4_out), .sel(and_1_out));
  Multiplexer #(.width(32), .enable("false")) multiplexer_5 (
    .in0(undriven), .in1(ula_1_saida), .sel(controle_1_mem_reg));  // open: out
  Multiplexer #(.width(32), .enable("false")) multiplexer_6 (
    .in0({instructionfetch_1_soma[31:28], instructionfetch_1__0_25, 2'b00}), .in1(multiplexer_4_out),
    .out(multiplexer_6_out), .sel(controle_1_jump));
  // also tied to GND on the sheet: {instructionfetch_1_soma[0], instructionfetch_1_soma[1], instructionfetch_1_soma[2], instructionfetch_1_soma[3], instructionfetch_1_soma[4], instructionfetch_1_soma[5], instructionfetch_1_soma[6], instructionfetch_1_soma[7], instructionfetch_1_soma[8], instructionfetch_1_soma[9], instructionfetch_1_soma[10], instructionfetch_1_soma[11], instructionfetch_1_soma[12], instructionfetch_1_soma[13], instructionfetch_1_soma[14], instructionfetch_1_soma[15], instructionfetch_1_soma[16], instructionfetch_1_soma[17], instructionfetch_1_soma[18], instructionfetch_1_soma[19], instructionfetch_1_soma[20], instructionfetch_1_soma[21], instructionfetch_1_soma[22], instructionfetch_1_soma[23], instructionfetch_1_soma[24], instructionfetch_1_soma[25], instructionfetch_1_soma[26], instructionfetch_1_soma[27]}
endmodule

module Registrador (
  input  in_1,
  input  [31:0] DIN,
  output [31:0] DOUT
);

  D_Flip_Flop d_ff_1 (.clk(in_1), .D(DIN[31]), .Q(DOUT[31]));  // open: Qn, preset, en, reset
  D_Flip_Flop d_ff_2 (.clk(in_1), .D(DIN[15]), .Q(DOUT[15]));  // open: Qn, preset, en, reset
  D_Flip_Flop d_ff_3 (.clk(in_1), .D(DIN[30]), .Q(DOUT[30]));  // open: Qn, preset, en, reset
  D_Flip_Flop d_ff_4 (.clk(in_1), .D(DIN[14]), .Q(DOUT[14]));  // open: Qn, preset, en, reset
  D_Flip_Flop d_ff_5 (.clk(in_1), .D(DIN[29]), .Q(DOUT[29]));  // open: Qn, preset, en, reset
  D_Flip_Flop d_ff_6 (.clk(in_1), .D(DIN[13]), .Q(DOUT[13]));  // open: Qn, preset, en, reset
  D_Flip_Flop d_ff_7 (.clk(in_1), .D(DIN[28]), .Q(DOUT[28]));  // open: Qn, preset, en, reset
  D_Flip_Flop d_ff_8 (.clk(in_1), .D(DIN[12]), .Q(DOUT[12]));  // open: Qn, preset, en, reset
  D_Flip_Flop d_ff_9 (.clk(in_1), .D(DIN[27]), .Q(DOUT[27]));  // open: Qn, preset, en, reset
  D_Flip_Flop d_ff_10 (.clk(in_1), .D(DIN[11]), .Q(DOUT[11]));  // open: Qn, preset, en, reset
  D_Flip_Flop d_ff_11 (.clk(in_1), .D(DIN[10]), .Q(DOUT[10]));  // open: Qn, preset, en, reset
  D_Flip_Flop d_ff_12 (.clk(in_1), .D(DIN[26]), .Q(DOUT[26]));  // open: Qn, preset, en, reset
  D_Flip_Flop d_ff_13 (.clk(in_1), .D(DIN[9]), .Q(DOUT[9]));  // open: Qn, preset, en, reset
  D_Flip_Flop d_ff_14 (.clk(in_1), .D(DIN[25]), .Q(DOUT[25]));  // open: Qn, preset, en, reset
  D_Flip_Flop d_ff_15 (.clk(in_1), .D(DIN[24]), .Q(DOUT[24]));  // open: Qn, preset, en, reset
  D_Flip_Flop d_ff_16 (.clk(in_1), .D(DIN[8]), .Q(DOUT[8]));  // open: Qn, preset, en, reset
  D_Flip_Flop d_ff_17 (.clk(in_1), .D(DIN[23]), .Q(DOUT[23]));  // open: Qn, preset, en, reset
  D_Flip_Flop d_ff_18 (.clk(in_1), .D(DIN[7]), .Q(DOUT[7]));  // open: Qn, preset, en, reset
  D_Flip_Flop d_ff_19 (.clk(in_1), .D(DIN[22]), .Q(DOUT[22]));  // open: Qn, preset, en, reset
  D_Flip_Flop d_ff_20 (.clk(in_1), .D(DIN[6]), .Q(DOUT[6]));  // open: Qn, preset, en, reset
  D_Flip_Flop d_ff_21 (.clk(in_1), .D(DIN[21]), .Q(DOUT[21]));  // open: Qn, preset, en, reset
  D_Flip_Flop d_ff_22 (.clk(in_1), .D(DIN[5]), .Q(DOUT[5]));  // open: Qn, preset, en, reset
  D_Flip_Flop d_ff_23 (.clk(in_1), .D(DIN[20]), .Q(DOUT[20]));  // open: Qn, preset, en, reset
  D_Flip_Flop d_ff_24 (.clk(in_1), .D(DIN[4]), .Q(DOUT[4]));  // open: Qn, preset, en, reset
  D_Flip_Flop d_ff_25 (.clk(in_1), .D(DIN[19]), .Q(DOUT[19]));  // open: Qn, preset, en, reset
  D_Flip_Flop d_ff_26 (.clk(in_1), .D(DIN[3]), .Q(DOUT[3]));  // open: Qn, preset, en, reset
  D_Flip_Flop d_ff_27 (.clk(in_1), .D(DIN[18]), .Q(DOUT[18]));  // open: Qn, preset, en, reset
  D_Flip_Flop d_ff_28 (.clk(in_1), .D(DIN[2]), .Q(DOUT[2]));  // open: Qn, preset, en, reset
  D_Flip_Flop d_ff_29 (.clk(in_1), .D(DIN[17]), .Q(DOUT[17]));  // open: Qn, preset, en, reset
  D_Flip_Flop d_ff_30 (.clk(in_1), .D(DIN[1]), .Q(DOUT[1]));  // open: Qn, preset, en, reset
  D_Flip_Flop d_ff_31 (.clk(in_1), .D(DIN[16]), .Q(DOUT[31]));  // open: Qn, preset, en, reset
  D_Flip_Flop d_ff_32 (.clk(in_1), .D(DIN[0]), .Q(DOUT[0]));  // open: Qn, preset, en, reset

  assign DOUT[16] = DOUT[31];
endmodule

module Banco_de_Registradores (
  input  [4:0] in_1,
  input  [4:0] in_2,
  input  [31:0] DATAIN,
  input  WRITER,
  input  [4:0] DadosDemux,
  output [31:0] RY,
  output [31:0] RX
);

  wire demultiplexer_1_out0, demultiplexer_1_out1, demultiplexer_1_out2, demultiplexer_1_out3,
       demultiplexer_1_out4, demultiplexer_1_out5, demultiplexer_1_out6, demultiplexer_1_out8,
       demultiplexer_1_out9, demultiplexer_1_out10, demultiplexer_1_out11, demultiplexer_1_out12,
       demultiplexer_1_out13, demultiplexer_1_out14, demultiplexer_1_out15, demultiplexer_1_out16,
       demultiplexer_1_out17, demultiplexer_1_out18, demultiplexer_1_out19, demultiplexer_1_out20,
       demultiplexer_1_out21, demultiplexer_1_out22, demultiplexer_1_out23, demultiplexer_1_out24,
       demultiplexer_1_out25, demultiplexer_1_out26, demultiplexer_1_out27, demultiplexer_1_out28,
       demultiplexer_1_out29, demultiplexer_1_out30, demultiplexer_1_out31;
  wire [31:0] registrador_1_dout, registrador_2_dout, registrador_3_dout, registrador_4_dout,
       registrador_5_dout, registrador_6_dout, registrador_7_dout, registrador_8_dout, registrador_9_dout,
       registrador_10_dout, registrador_11_dout, registrador_12_dout, registrador_13_dout,
       registrador_14_dout, registrador_15_dout, registrador_16_dout, registrador_17_dout,
       registrador_18_dout, registrador_19_dout, registrador_20_dout, registrador_21_dout,
       registrador_22_dout, registrador_23_dout, registrador_24_dout, registrador_25_dout,
       registrador_26_dout, registrador_27_dout, registrador_28_dout, registrador_29_dout,
       registrador_30_dout, registrador_31_dout, registrador_32_dout;

  Multiplexer #(.select(5), .width(32), .enable("false")) multiplexer_1 (
    .in0(registrador_32_dout), .in1(registrador_31_dout), .in2(registrador_30_dout),
    .in3(registrador_28_dout), .in4(registrador_26_dout), .in5(registrador_24_dout),
    .in6(registrador_22_dout), .in7(registrador_20_dout), .in8(registrador_18_dout),
    .in9(registrador_16_dout), .in10(registrador_14_dout), .in11(registrador_12_dout),
    .in12(registrador_10_dout), .in13(registrador_8_dout), .in14(registrador_6_dout),
    .in15(registrador_4_dout), .in16(registrador_29_dout), .in17(registrador_27_dout),
    .in18(registrador_25_dout), .in19(registrador_23_dout), .in20(registrador_21_dout),
    .in21(registrador_19_dout), .in22(registrador_17_dout), .in23(registrador_15_dout),
    .in24(registrador_13_dout), .in25(registrador_11_dout), .in26(registrador_9_dout),
    .in27(registrador_7_dout), .in28(registrador_5_dout), .in29(registrador_3_dout),
    .in30(registrador_2_dout), .in31(registrador_1_dout), .out(RY), .sel(in_1));
  Multiplexer #(.select(5), .width(32), .enable("false")) multiplexer_2 (
    .in0(registrador_32_dout), .in1(registrador_31_dout), .in2(registrador_30_dout),
    .in3(registrador_28_dout), .in4(registrador_26_dout), .in5(registrador_24_dout),
    .in6(registrador_22_dout), .in7(registrador_20_dout), .in8(registrador_18_dout),
    .in9(registrador_16_dout), .in10(registrador_14_dout), .in11(registrador_12_dout),
    .in12(registrador_10_dout), .in13(registrador_8_dout), .in14(registrador_6_dout),
    .in15(registrador_4_dout), .in16(registrador_29_dout), .in17(registrador_27_dout),
    .in18(registrador_25_dout), .in19(registrador_23_dout), .in20(registrador_21_dout),
    .in21(registrador_19_dout), .in22(registrador_17_dout), .in23(registrador_15_dout),
    .in24(registrador_13_dout), .in25(registrador_11_dout), .in26(registrador_9_dout),
    .in27(registrador_7_dout), .in28(registrador_5_dout), .in29(registrador_3_dout),
    .in30(registrador_2_dout), .in31(registrador_1_dout), .out(RX), .sel(in_2));
  Demultiplexer #(.select(5), .enable("false")) demultiplexer_1 (
    .out0(demultiplexer_1_out0), .out1(demultiplexer_1_out1), .out2(demultiplexer_1_out2),
    .out3(demultiplexer_1_out3), .out4(demultiplexer_1_out4), .out5(demultiplexer_1_out5),
    .out6(demultiplexer_1_out6), .out7(demultiplexer_1_out6), .out8(demultiplexer_1_out8),
    .out9(demultiplexer_1_out9), .out10(demultiplexer_1_out10), .out11(demultiplexer_1_out11),
    .out12(demultiplexer_1_out12), .out13(demultiplexer_1_out13), .out14(demultiplexer_1_out14),
    .out15(demultiplexer_1_out15), .out16(demultiplexer_1_out16), .out17(demultiplexer_1_out17),
    .out18(demultiplexer_1_out18), .out19(demultiplexer_1_out19), .out20(demultiplexer_1_out20),
    .out21(demultiplexer_1_out21), .out22(demultiplexer_1_out22), .out23(demultiplexer_1_out23),
    .out24(demultiplexer_1_out24), .out25(demultiplexer_1_out25), .out26(demultiplexer_1_out26),
    .out27(demultiplexer_1_out27), .out28(demultiplexer_1_out28), .out29(demultiplexer_1_out29),
    .out30(demultiplexer_1_out30), .out31(demultiplexer_1_out31), .in(WRITER), .sel(DadosDemux));
  Registrador registrador_1 (.in_1(demultiplexer_1_out31), .DIN(DATAIN), .DOUT(registrador_1_dout));
  Registrador registrador_2 (.in_1(demultiplexer_1_out30), .DIN(DATAIN), .DOUT(registrador_2_dout));
  Registrador registrador_3 (.in_1(demultiplexer_1_out29), .DIN(DATAIN), .DOUT(registrador_3_dout));
  Registrador registrador_4 (.in_1(demultiplexer_1_out15), .DIN(DATAIN), .DOUT(registrador_4_dout));
  Registrador registrador_5 (.in_1(demultiplexer_1_out28), .DIN(DATAIN), .DOUT(registrador_5_dout));
  Registrador registrador_6 (.in_1(demultiplexer_1_out14), .DIN(DATAIN), .DOUT(registrador_6_dout));
  Registrador registrador_7 (.in_1(demultiplexer_1_out27), .DIN(DATAIN), .DOUT(registrador_7_dout));
  Registrador registrador_8 (.in_1(demultiplexer_1_out13), .DIN(DATAIN), .DOUT(registrador_8_dout));
  Registrador registrador_9 (.in_1(demultiplexer_1_out26), .DIN(DATAIN), .DOUT(registrador_9_dout));
  Registrador registrador_10 (.in_1(demultiplexer_1_out12), .DIN(DATAIN), .DOUT(registrador_10_dout));
  Registrador registrador_11 (.in_1(demultiplexer_1_out25), .DIN(DATAIN), .DOUT(registrador_11_dout));
  Registrador registrador_12 (.in_1(demultiplexer_1_out11), .DIN(DATAIN), .DOUT(registrador_12_dout));
  Registrador registrador_13 (.in_1(demultiplexer_1_out24), .DIN(DATAIN), .DOUT(registrador_13_dout));
  Registrador registrador_14 (.in_1(demultiplexer_1_out10), .DIN(DATAIN), .DOUT(registrador_14_dout));
  Registrador registrador_15 (.in_1(demultiplexer_1_out23), .DIN(DATAIN), .DOUT(registrador_15_dout));
  Registrador registrador_16 (.in_1(demultiplexer_1_out9), .DIN(DATAIN), .DOUT(registrador_16_dout));
  Registrador registrador_17 (.in_1(demultiplexer_1_out22), .DIN(DATAIN), .DOUT(registrador_17_dout));
  Registrador registrador_18 (.in_1(demultiplexer_1_out8), .DIN(DATAIN), .DOUT(registrador_18_dout));
  Registrador registrador_19 (.in_1(demultiplexer_1_out21), .DIN(DATAIN), .DOUT(registrador_19_dout));
  Registrador registrador_20 (.in_1(demultiplexer_1_out6), .DIN(DATAIN), .DOUT(registrador_20_dout));
  Registrador registrador_21 (.in_1(demultiplexer_1_out20), .DIN(DATAIN), .DOUT(registrador_21_dout));
  Registrador registrador_22 (.in_1(demultiplexer_1_out6), .DIN(DATAIN), .DOUT(registrador_22_dout));
  Registrador registrador_23 (.in_1(demultiplexer_1_out19), .DIN(DATAIN), .DOUT(registrador_23_dout));
  Registrador registrador_24 (.in_1(demultiplexer_1_out5), .DIN(DATAIN), .DOUT(registrador_24_dout));
  Registrador registrador_25 (.in_1(demultiplexer_1_out18), .DIN(DATAIN), .DOUT(registrador_25_dout));
  Registrador registrador_26 (.in_1(demultiplexer_1_out4), .DIN(DATAIN), .DOUT(registrador_26_dout));
  Registrador registrador_27 (.in_1(demultiplexer_1_out17), .DIN(DATAIN), .DOUT(registrador_27_dout));
  Registrador registrador_28 (.in_1(demultiplexer_1_out3), .DIN(DATAIN), .DOUT(registrador_28_dout));
  Registrador registrador_29 (.in_1(demultiplexer_1_out16), .DIN(DATAIN), .DOUT(registrador_29_dout));
  Registrador registrador_30 (.in_1(demultiplexer_1_out2), .DIN(DATAIN), .DOUT(registrador_30_dout));
  Registrador registrador_31 (.in_1(demultiplexer_1_out1), .DIN(DATAIN), .DOUT(registrador_31_dout));
  Registrador registrador_32 (.in_1(demultiplexer_1_out0), .DIN(DATAIN), .DOUT(registrador_32_dout));
endmodule

module ULA (
  input  [31:0] x,
  input  [2:0] MUX,
  input  [31:0] y,
  output out_4,
  output [31:0] saida
);

  wire [31:0] adder_1_out, and_1_out, or_1_out, subtractor_1_out;

  Adder #(.width(32)) adder_1 (.a(x), .b(y), .out(adder_1_out));  // open: cin, cout
  Subtractor #(.width(32)) subtractor_1 (.a(x), .b(y), .out(subtractor_1_out));  // open: bin, bout
  assign and_1_out = x & y;  // AND_Gate and_1, 32 bits wide
  assign or_1_out = x | y;  // OR_Gate or_1, 32 bits wide
  Multiplexer #(.select(3), .width(32), .enable("false")) multiplexer_1 (
    .in2(adder_1_out), .in4(subtractor_1_out), .in5(and_1_out), .in6(or_1_out), .out(saida), .sel(MUX));  // open: in0, in1, in3, in7
  nor nor_1 (out_4, saida[0], saida[1], saida[2], saida[3], saida[4], saida[5], saida[6], saida[7], saida[8], saida[9], saida[10], saida[11], saida[12], saida[13], saida[14], saida[15], saida[16], saida[17], saida[18], saida[19], saida[20], saida[21], saida[22], saida[23], saida[24], saida[25], saida[26], saida[27], saida[28], saida[29], saida[30], saida[31]);

  // Notes on the sheet:
  //   10-- e
  //   11 - ou
  //   00 - soma
  //   01 - subtraçao
endmodule

module Controle (
  input  [5:0] in_1,
  output RegDST,
  output ALUsrc,
  output mem_reg,
  output escrita_reg,
  output leitura_mem,
  output Escrita_Mem,
  output Branch,
  output OpALU1,
  output OpALU0,
  output JUMP
);

  and and_1 (OpALU1, ~in_1[0], ~in_1[1], ~in_1[2], ~in_1[3], ~in_1[4], ~in_1[4]);  // AND_Gate
  and and_2 (leitura_mem, in_1[0], ~in_1[1], ~in_1[2], ~in_1[3], in_1[4], in_1[5]);  // AND_Gate
  and and_3 (Escrita_Mem, in_1[0], ~in_1[1], in_1[2], ~in_1[3], in_1[4], in_1[5]);  // AND_Gate
  and and_4 (Branch, ~in_1[0], ~in_1[1], ~in_1[2], in_1[3], ~in_1[4], ~in_1[5]);  // AND_Gate
  or or_1 (ALUsrc, leitura_mem, Escrita_Mem);
  or or_2 (escrita_reg, OpALU1, leitura_mem);
  and and_5 (JUMP, ~in_1[0], in_1[1], ~in_1[2], ~in_1[3], ~in_1[4], ~in_1[5]);  // AND_Gate

  assign mem_reg = leitura_mem;
  assign OpALU0 = Branch;
  assign RegDST = OpALU1;

  // Notes on the sheet:
  //   Op5
  //   Op4
  //   Op3
  //   Op2
  //   Op1
  //   Op0
  //   R
  //   lw
  //   sw
  //   beq
endmodule

module Memoria_de_Dados (
  input  [31:0] in_1,
  input  R_W,
  input  [31:0] saida
);

  wire clock_out;
  wire [31:0] adder_1_out;

  Clock clock (.out(clock_out));
  Register #(.width(32)) register_1 (.D(adder_1_out), .en(R_W), .Q(saida), .clk(clock_out), .clr(1'b0));
  Adder #(.width(32)) adder_1 (.a(in_1), .b(saida), .out(adder_1_out));  // open: cin, cout
  RAM #(.addrWidth(16), .dataWidth(32)) ram_1 (.addr(saida[15:0]));  // open: data, sel, clk, ld, clr
  RAM #(.addrWidth(16), .dataWidth(32)) ram_2 (.addr(saida[31:16]));  // open: data, sel, clk, ld, clr
endmodule

module ControleULA (
  input  in_1,
  input  in_2,
  input  [5:0] in_3,
  output [2:0] out_4
);

  wire and_1_out, or_1_out;

  or or_1 (or_1_out, in_3[0], in_3[3]);
  and and_1 (and_1_out, in_3[1], in_2);
  and and_2 (out_4[0], or_1_out, in_2);
  or or_2 (out_4[2], and_1_out, in_1);
  or or_3 (out_4[1], ~in_2, ~in_3[2]);  // OR_Gate

  assign in_3[4] = in_3[5];
  // also tied to GND on the sheet: in_3[5]
endmodule
